// Logisim project calculatorCPU.circ as structural Verilog: 16 circuits, main circuit main
module main (
);

  wire _0_out, _1_out, _2_out, _3_out, _4_out, _5_out, _6_out, _7_out, _8_out, _9_out, ALU_zero, BEQ_out,
       BNE_out, button_2_out, button_3_out, button_4_out, button_5_out, button_out, C_out, clock_1_out,
       Control_Unit_alu_source, Control_Unit_branch_equal, Control_Unit_branch_not_equal, Control_Unit_jump,
       Control_Unit_register_destination, Control_Unit_register_write, keypad_controller_1_write, not_1_out,
       or_1_out;
  wire [1:0] ALU_Control_shift_operation, Control_Unit_alu_operation;
  wire [2:0] lcd_controller_1__7_segment_2_2, lcd_controller_1__7_segment_4_2,
       lcd_controller_1__7_segment_5_2, lcd_controller_1__7_segment_6_2, lcd_controller_1__7_segment_8_2,
       lcd_controller_1_minus_2;
  wire [3:0] ALU_Control_alu_operation, lcd_controller_1__7_segment_2, lcd_controller_1__7_segment_4,
       lcd_controller_1__7_segment_5, lcd_controller_1__7_segment_6, lcd_controller_1__7_segment_8,
       lcd_controller_1_minus;
  wire [4:0] Instruction_Memory_output_2, multiplexer_2_out;
  wire [5:0] Control_Unit_immediate_functions, multiplexer_1_out;
  wire [6:0] lcd_controller_1__7_segment_0, lcd_controller_1__7_segment_1, lcd_controller_1__7_segment_3,
       lcd_controller_1__7_segment_7, lcd_controller_1__7_segment_9;
  wire [27:0] adder_1_out;
  wire [31:0] adder_2_out, ALU_result, Instruction_Memory_output, keypad_controller_1_output,
       multiplexer_3_out, multiplexer_4_out, multiplexer_5_out, PC_q, Register_read_data_1,
       Register_read_data_2, Register_t8, Register_t9, Shift_Left_Two_2_result, Shift_Left_Two_result_2,
       Sign_Extend__32_bit_result;
  wire [31:28] Shift_Left_Two_result;

  Register #(.width(32)) PC (.D(multiplexer_5_out), .Q(PC_q), .clk(clock_1_out));  // open: en, clr
  Clock clock_1 (.out(clock_1_out));
  Adder #(.width(32)) adder_1 (
    .a(PC_q), .b(32'h4), .out({Shift_Left_Two_result_2[31:28], adder_1_out}));  // open: cin, cout
  Instruction_Memory__TO_DO Instruction_Memory (
    .Input(PC_q),
    .Output({Instruction_Memory_output[31:11], Instruction_Memory_output_2, Instruction_Memory_output[5:0]}));
  Sign_Extend__TO_DO Sign_Extend (
    ._16_Bit_Input({Instruction_Memory_output[15:11], Instruction_Memory_output_2, Instruction_Memory_output[5:0]}),
    ._32_Bit_Result(Sign_Extend__32_bit_result));
  Multiplexer #(.width(6), .enable("false")) multiplexer_1 (
    .in0(Instruction_Memory_output[5:0]), .in1(Control_Unit_immediate_functions), .out(multiplexer_1_out),
    .sel(Control_Unit_alu_source));
  Shift_Left_Two Shift_Left_Two (
    .Input({Instruction_Memory_output[31:11], Instruction_Memory_output_2, Instruction_Memory_output[5:0]}),
    .Result({Shift_Left_Two_result, Shift_Left_Two_result_2[27:0]}));
  Multiplexer #(.width(5), .enable("false")) multiplexer_2 (
    .in0(Instruction_Memory_output[20:16]), .in1(Instruction_Memory_output[15:11]), .out(multiplexer_2_out),
    .sel(Control_Unit_register_destination));
  Shift_Left_Two Shift_Left_Two_2 (.Input(Sign_Extend__32_bit_result), .Result(Shift_Left_Two_2_result));
  Control_Unit__TO_DO Control_Unit (
    .Opcode(Instruction_Memory_output[31:26]), .Register_Destination(Control_Unit_register_destination),
    .Jump(Control_Unit_jump), .Branch_Not_Equal(Control_Unit_branch_not_equal),
    .ALU_Operation(Control_Unit_alu_operation), .ALU_Source(Control_Unit_alu_source),
    .Register_Write(Control_Unit_register_write), .Immediate_Functions(Control_Unit_immediate_functions),
    .Branch_Equal(Control_Unit_branch_equal));
  Register_File__TO_DO Register (
    .Read_Data_1(Register_read_data_1), .t8(Register_t8), .t9(Register_t9),
    .Read_Data_2(Register_read_data_2), .RegWrite(Control_Unit_register_write),
    .Write_Register(multiplexer_2_out), .Write_Data___t9(keypad_controller_1_output),
    .Write_Signal(keypad_controller_1_write), .Write_Data(ALU_result),
    .Read_Register_1(Instruction_Memory_output[25:21]), .Read_Register_2(Instruction_Memory_output[20:16]),
    .Clock(clock_1_out));
  ALU_Control ALU_Control (
    .Function(multiplexer_1_out), .Shift_Operation(ALU_Control_shift_operation),
    .ALU_Operation_Input(Control_Unit_alu_operation), .ALU_Operation(ALU_Control_alu_operation));
  Adder #(.width(32)) adder_2 (
    .a({Shift_Left_Two_result_2[31:28], adder_1_out}), .b(Shift_Left_Two_2_result), .out(adder_2_out));  // open: cin, cout
  Multiplexer #(.width(32), .enable("false")) multiplexer_3 (
    .in0(Register_read_data_2), .in1(Sign_Extend__32_bit_result), .out(multiplexer_3_out),
    .sel(Control_Unit_alu_source));
  Multiplexer #(.width(32), .enable("false")) multiplexer_4 (
    .in0({Shift_Left_Two_result_2[31:28], adder_1_out}), .in1(adder_2_out), .out(multiplexer_4_out),
    .sel(or_1_out));
  not not_1 (not_1_out, ALU_zero);
  Multiplexer #(.width(32), .enable("false")) multiplexer_5 (
    .in0(multiplexer_4_out), .in1(Shift_Left_Two_result_2), .out(multiplexer_5_out), .sel(Control_Unit_jump));
  and BEQ (BEQ_out, Control_Unit_branch_equal, ALU_zero);
  and BNE (BNE_out, not_1_out, Control_Unit_branch_not_equal);
  _32_bit_ALU__TO_DO ALU (
    .Input_1(Register_read_data_1), .Input_2(multiplexer_3_out), .Shift_Amount(Instruction_Memory_output_2),
    .Shift_Operation(ALU_Control_shift_operation), .Zero(ALU_zero), .Result(ALU_result),
    .ALU_Operation(ALU_Control_alu_operation));
  or or_1 (or_1_out, BEQ_out, BNE_out);
  _7_Segment_Display u_7_segment_display_1 (
    .g(lcd_controller_1_minus[0]), .f(lcd_controller_1_minus[1]), .a(lcd_controller_1_minus[2]),
    .b(lcd_controller_1_minus[3]), .e(lcd_controller_1_minus_2[0]), .d(lcd_controller_1_minus_2[1]),
    .c(lcd_controller_1_minus_2[2]));  // open: dp
  LCD_Controller lcd_controller_1 (
    .From__t8(Register_t8), .Minus({lcd_controller_1_minus_2, lcd_controller_1_minus}),
    ._7_Segment_9(lcd_controller_1__7_segment_9),
    ._7_Segment_8({lcd_controller_1__7_segment_8_2, lcd_controller_1__7_segment_8}),
    ._7_Segment_7(lcd_controller_1__7_segment_7),
    ._7_Segment_6({lcd_controller_1__7_segment_6_2, lcd_controller_1__7_segment_6}),
    ._7_Segment_5({lcd_controller_1__7_segment_5_2, lcd_controller_1__7_segment_5}),
    ._7_Segment_4({lcd_controller_1__7_segment_4_2, lcd_controller_1__7_segment_4}),
    ._7_Segment_3(lcd_controller_1__7_segment_3),
    ._7_Segment_2({lcd_controller_1__7_segment_2_2, lcd_controller_1__7_segment_2}),
    ._7_Segment_1(lcd_controller_1__7_segment_1), ._7_Segment_0(lcd_controller_1__7_segment_0));
  Keypad_Controller keypad_controller_1 (
    .C(C_out), .in_2(button_out), .in_3(button_5_out), .in_4(button_4_out), .in_5(button_3_out),
    .in_6(button_2_out), ._9(_9_out), ._8(_8_out), ._7(_7_out), ._6(_6_out), ._5(_5_out), ._4(_4_out),
    ._3(_3_out), ._2(_2_out), ._1(_1_out), ._0(_0_out), .From__t9(Register_t9),
    .Write(keypad_controller_1_write), .Output(keypad_controller_1_output));
  _7_Segment_Display u_7_segment_display_2 (
    .g(lcd_controller_1__7_segment_9[0]), .f(lcd_controller_1__7_segment_9[1]),
    .a(lcd_controller_1__7_segment_9[2]), .b(lcd_controller_1__7_segment_9[3]),
    .e(lcd_controller_1__7_segment_9[4]), .d(lcd_controller_1__7_segment_9[5]),
    .c(lcd_controller_1__7_segment_9[6]));  // open: dp
  _7_Segment_Display u_7_segment_display_3 (
    .g(lcd_controller_1__7_segment_8[0]), .f(lcd_controller_1__7_segment_8[1]),
    .a(lcd_controller_1__7_segment_8[2]), .b(lcd_controller_1__7_segment_8[3]),
    .e(lcd_controller_1__7_segment_8_2[0]), .d(lcd_controller_1__7_segment_8_2[1]),
    .c(lcd_controller_1__7_segment_8_2[2]));  // open: dp
  _7_Segment_Display u_7_segment_display_4 (
    .g(lcd_controller_1__7_segment_7[0]), .f(lcd_controller_1__7_segment_7[1]),
    .a(lcd_controller_1__7_segment_7[2]), .b(lcd_controller_1__7_segment_7[3]),
    .e(lcd_controller_1__7_segment_7[4]), .d(lcd_controller_1__7_segment_7[5]),
    .c(lcd_controller_1__7_segment_7[6]));  // open: dp
  _7_Segment_Display u_7_segment_display_5 (
    .g(lcd_controller_1__7_segment_6[0]), .f(lcd_controller_1__7_segment_6[1]),
    .a(lcd_controller_1__7_segment_6[2]), .b(lcd_controller_1__7_segment_6[3]),
    .e(lcd_controller_1__7_segment_6_2[0]), .d(lcd_controller_1__7_segment_6_2[1]),
    .c(lcd_controller_1__7_segment_6_2[2]));  // open: dp
  _7_Segment_Display u_7_segment_display_6 (
    .g(lcd_controller_1__7_segment_4[0]), .f(lcd_controller_1__7_segment_4[1]),
    .a(lcd_controller_1__7_segment_4[2]), .b(lcd_controller_1__7_segment_4[3]),
    .e(lcd_controller_1__7_segment_4_2[0]), .d(lcd_controller_1__7_segment_4_2[1]),
    .c(lcd_controller_1__7_segment_4_2[2]));  // open: dp
  _7_Segment_Display u_7_segment_display_7 (
    .g(lcd_controller_1__7_segment_5[0]), .f(lcd_controller_1__7_segment_5[1]),
    .a(lcd_controller_1__7_segment_5[2]), .b(lcd_controller_1__7_segment_5[3]),
    .e(lcd_controller_1__7_segment_5_2[0]), .d(lcd_controller_1__7_segment_5_2[1]),
    .c(lcd_controller_1__7_segment_5_2[2]));  // open: dp
  Button _7 (.out(_7_out));
  Button _4 (.out(_4_out));
  Button _1 (.out(_1_out));
  Button _0 (.out(_0_out));
  _7_Segment_Display u_7_segment_display_8 (
    .g(lcd_controller_1__7_segment_3[0]), .f(lcd_controller_1__7_segment_3[1]),
    .a(lcd_controller_1__7_segment_3[2]), .b(lcd_controller_1__7_segment_3[3]),
    .e(lcd_controller_1__7_segment_3[4]), .d(lcd_controller_1__7_segment_3[5]),
    .c(lcd_controller_1__7_segment_3[6]));  // open: dp
  _7_Segment_Display u_7_segment_display_9 (
    .g(lcd_controller_1__7_segment_2[0]), .f(lcd_controller_1__7_segment_2[1]),
    .a(lcd_controller_1__7_segment_2[2]), .b(lcd_controller_1__7_segment_2[3]),
    .e(lcd_controller_1__7_segment_2_2[0]), .d(lcd_controller_1__7_segment_2_2[1]),
    .c(lcd_controller_1__7_segment_2_2[2]));  // open: dp
  Button _8 (.out(_8_out));
  Button _5 (.out(_5_out));
  Button _2 (.out(_2_out));
  Button C (.out(C_out));
  _7_Segment_Display u_7_segment_display_10 (
    .g(lcd_controller_1__7_segment_0[0]), .f(lcd_controller_1__7_segment_0[1]),
    .a(lcd_controller_1__7_segment_0[2]), .b(lcd_controller_1__7_segment_0[3]),
    .e(lcd_controller_1__7_segment_0[4]), .d(lcd_controller_1__7_segment_0[5]),
    .c(lcd_controller_1__7_segment_0[6]));  // open: dp
  _7_Segment_Display u_7_segment_display_11 (
    .g(lcd_controller_1__7_segment_1[0]), .f(lcd_controller_1__7_segment_1[1]),
    .a(lcd_controller_1__7_segment_1[2]), .b(lcd_controller_1__7_segment_1[3]),
    .e(lcd_controller_1__7_segment_1[4]), .d(lcd_controller_1__7_segment_1[5]),
    .c(lcd_controller_1__7_segment_1[6]));  // open: dp
  Button _9 (.out(_9_out));
  Button _6 (.out(_6_out));
  Button _3 (.out(_3_out));
  Button button (.out(button_out));
  Button button_2 (.out(button_2_out));
  Button button_3 (.out(button_3_out));
  Button button_4 (.out(button_4_out));
  Button button_5 (.out(button_5_out));

  // Notes on the sheet:
  //   Write Data to $t9
  //   Write Signal for $t9
  //   From $t8
  //   From $t9
endmodule

module LCD_Controller (
  input  [31:0] From__t8,
  output [6:0] Minus,
  output [6:0] _7_Segment_9,
  output [6:0] _7_Segment_8,
  output [6:0] _7_Segment_7,
  output [6:0] _7_Segment_6,
  output [6:0] _7_Segment_5,
  output [6:0] _7_Segment_4,
  output [6:0] _7_Segment_3,
  output [6:0] _7_Segment_2,
  output [6:0] _7_Segment_1,
  output [6:0] _7_Segment_0
);

  wire [3:0] binarytobcd_1_bcd0, binarytobcd_1_bcd1, binarytobcd_1_bcd2, binarytobcd_1_bcd3,
       binarytobcd_1_bcd4, binarytobcd_1_bcd5, binarytobcd_1_bcd6, binarytobcd_1_bcd7, binarytobcd_1_bcd8,
       binarytobcd_1_bcd9;

  BinaryToBCD binarytobcd_1 (
    .Input(From__t8), .Minus(Minus[0]), .BCD9(binarytobcd_1_bcd9), .BCD8(binarytobcd_1_bcd8),
    .BCD7(binarytobcd_1_bcd7), .BCD6(binarytobcd_1_bcd6), .BCD5(binarytobcd_1_bcd5),
    .BCD4(binarytobcd_1_bcd4), .BCD3(binarytobcd_1_bcd3), .BCD2(binarytobcd_1_bcd2),
    .BCD1(binarytobcd_1_bcd1), .BCD0(binarytobcd_1_bcd0));
  _7_Segment_Controller u_7_segment_controller_1 (.BCD(binarytobcd_1_bcd9), .out_2(_7_Segment_9));
  _7_Segment_Controller u_7_segment_controller_2 (.BCD(binarytobcd_1_bcd8), .out_2(_7_Segment_8));
  _7_Segment_Controller u_7_segment_controller_3 (.BCD(binarytobcd_1_bcd7), .out_2(_7_Segment_7));
  _7_Segment_Controller u_7_segment_controller_4 (.BCD(binarytobcd_1_bcd6), .out_2(_7_Segment_6));
  _7_Segment_Controller u_7_segment_controller_5 (.BCD(binarytobcd_1_bcd5), .out_2(_7_Segment_5));
  _7_Segment_Controller u_7_segment_controller_6 (.BCD(binarytobcd_1_bcd4), .out_2(_7_Segment_4));
  _7_Segment_Controller u_7_segment_controller_7 (.BCD(binarytobcd_1_bcd3), .out_2(_7_Segment_3));
  _7_Segment_Controller u_7_segment_controller_8 (.BCD(binarytobcd_1_bcd2), .out_2(_7_Segment_2));
  _7_Segment_Controller u_7_segment_controller_9 (.BCD(binarytobcd_1_bcd1), .out_2(_7_Segment_1));
  _7_Segment_Controller u_7_segment_controller_10 (.BCD(binarytobcd_1_bcd0), .out_2(_7_Segment_0));

  assign Minus[6:1] = {6{1'b0}};
endmodule

module _7_Segment_Controller (
  input  [3:0] BCD,
  output [6:0] out_2
);

  wire and_1_out, and_2_out, and_3_out, and_4_out, and_5_out, and_6_out, and_7_out, and_8_out, and_9_out,
       and_10_out, and_11_out, and_12_out, and_13_out, and_14_out, and_15_out, and_16_out, not_1_out,
       not_2_out, not_3_out, not_4_out, not_5_out, not_6_out, not_7_out, not_8_out, not_9_out, not_10_out,
       not_11_out, not_12_out, not_13_out, not_14_out, not_15_out, not_16_out, not_17_out, not_18_out,
       not_19_out, not_20_out, not_21_out;

  not not_1 (not_1_out, BCD[2]);
  not not_2 (not_2_out, BCD[0]);
  not not_3 (not_3_out, BCD[1]);
  not not_4 (not_4_out, BCD[1]);
  not not_5 (not_5_out, BCD[0]);
  not not_6 (not_6_out, BCD[1]);
  not not_7 (not_7_out, BCD[0]);
  not not_8 (not_8_out, BCD[2]);
  not not_9 (not_9_out, BCD[0]);
  not not_10 (not_10_out, BCD[1]);
  not not_11 (not_11_out, BCD[0]);
  not not_12 (not_12_out, BCD[2]);
  not not_13 (not_13_out, BCD[0]);
  not not_14 (not_14_out, BCD[0]);
  not not_15 (not_15_out, BCD[2]);
  not not_16 (not_16_out, BCD[0]);
  not not_17 (not_17_out, BCD[2]);
  not not_18 (not_18_out, BCD[0]);
  not not_19 (not_19_out, BCD[1]);
  not not_20 (not_20_out, BCD[1]);
  and and_1 (and_1_out, not_1_out, BCD[1]);
  and and_2 (and_2_out, BCD[1], not_2_out);
  and and_3 (and_3_out, BCD[2], not_3_out);
  and and_4 (and_4_out, not_4_out, not_5_out);
  and and_5 (and_5_out, BCD[2], not_6_out);
  and and_6 (and_6_out, BCD[2], not_7_out);
  and and_7 (and_7_out, not_8_out, not_9_out);
  and and_8 (and_8_out, BCD[2], BCD[0]);
  not not_21 (not_21_out, BCD[2]);
  and and_9 (and_9_out, not_10_out, not_11_out);
  and and_10 (and_10_out, BCD[1], BCD[0]);
  and and_11 (and_11_out, not_12_out, not_13_out);
  and and_12 (and_12_out, BCD[1], not_14_out);
  and and_13 (and_13_out, not_15_out, not_16_out);
  and and_14 (and_14_out, not_17_out, BCD[1]);
  and and_15 (and_15_out, BCD[1], not_18_out);
  and and_16 (and_16_out, BCD[2], not_19_out, BCD[0]);
  or or_1 (out_2[6], not_20_out, BCD[0], BCD[2]);
  or or_2 (out_2[0], and_1_out, and_2_out, and_3_out, BCD[3]);
  or or_3 (out_2[1], and_4_out, and_5_out, and_6_out, BCD[3]);
  or or_4 (out_2[2], and_7_out, BCD[1], and_8_out, BCD[3]);
  or or_5 (out_2[3], not_21_out, and_9_out, and_10_out);
  or or_6 (out_2[4], and_11_out, and_12_out);
  or or_7 (out_2[5], and_13_out, and_14_out, and_15_out, and_16_out);
endmodule

module BinaryToBCD (
  input  [31:0] Input,
  output Minus,
  output [3:0] BCD9,
  output [3:0] BCD8,
  output [3:0] BCD7,
  output [3:0] BCD6,
  output [3:0] BCD5,
  output [3:0] BCD4,
  output [3:0] BCD3,
  output [3:0] BCD2,
  output [3:0] BCD1,
  output [3:0] BCD0
);

  wire [27:0] subtractor_1_out, subtractor_2_out, subtractor_3_out, subtractor_4_out, subtractor_5_out,
       subtractor_6_out, subtractor_7_out, subtractor_8_out, subtractor_9_out;
  wire [31:0] adder_1_out, divider_1_out, divider_2_out, divider_3_out, divider_4_out, divider_5_out,
       divider_6_out, divider_7_out, divider_8_out, multiplexer_1_out, multiplier_1_out, multiplier_2_out,
       multiplier_3_out, multiplier_4_out, multiplier_5_out, multiplier_6_out, multiplier_7_out,
       multiplier_8_out, multiplier_9_out, not_1_out;
  wire [31:4] divider_9_out;

  assign not_1_out = ~Input;  // NOT_Gate not_1, 32 bits wide
  Adder #(.width(32)) adder_1 (.a(not_1_out), .b(32'h1), .out(adder_1_out));  // open: cin, cout
  Multiplexer #(.width(32)) multiplexer_1 (
    .in0(Input), .in1(adder_1_out), .out(multiplexer_1_out), .sel(Input[31]));  // open: en
  Subtractor #(.width(32)) subtractor_1 (
    .a(multiplexer_1_out), .b(multiplier_1_out), .out({subtractor_1_out, BCD0}));  // open: bin, bout
  Multiplier #(.width(32)) multiplier_1 (.a(divider_1_out), .b(32'ha), .out(multiplier_1_out));  // open: cin, cout
  Divider #(.width(32)) divider_1 (.a(multiplexer_1_out), .b(32'ha), .out(divider_1_out));  // open: upper, rem
  Subtractor #(.width(32)) subtractor_2 (
    .a(divider_1_out), .b(multiplier_2_out), .out({subtractor_2_out, BCD1}));  // open: bin, bout
  Multiplier #(.width(32)) multiplier_2 (.a(divider_2_out), .b(32'ha), .out(multiplier_2_out));  // open: cin, cout
  Divider #(.width(32)) divider_2 (.a(divider_1_out), .b(32'ha), .out(divider_2_out));  // open: upper, rem
  Subtractor #(.width(32)) subtractor_3 (
    .a(divider_2_out), .b(multiplier_3_out), .out({subtractor_3_out, BCD2}));  // open: bin, bout
  Multiplier #(.width(32)) multiplier_3 (.a(divider_3_out), .b(32'ha), .out(multiplier_3_out));  // open: cin, cout
  Divider #(.width(32)) divider_3 (.a(divider_2_out), .b(32'ha), .out(divider_3_out));  // open: upper, rem
  Subtractor #(.width(32)) subtractor_4 (
    .a(divider_3_out), .b(multiplier_4_out), .out({subtractor_4_out, BCD3}));  // open: bin, bout
  Multiplier #(.width(32)) multiplier_4 (.a(divider_4_out), .b(32'ha), .out(multiplier_4_out));  // open: cin, cout
  Divider #(.width(32)) divider_4 (.a(divider_3_out), .b(32'ha), .out(divider_4_out));  // open: upper, rem
  Subtractor #(.width(32)) subtractor_5 (
    .a(divider_4_out), .b(multiplier_5_out), .out({subtractor_5_out, BCD4}));  // open: bin, bout
  Multiplier #(.width(32)) multiplier_5 (.a(divider_5_out), .b(32'ha), .out(multiplier_5_out));  // open: cin, cout
  Divider #(.width(32)) divider_5 (.a(divider_4_out), .b(32'ha), .out(divider_5_out));  // open: upper, rem
  Subtractor #(.width(32)) subtractor_6 (
    .a(divider_5_out), .b(multiplier_6_out), .out({subtractor_6_out, BCD5}));  // open: bin, bout
  Multiplier #(.width(32)) multiplier_6 (.a(divider_6_out), .b(32'ha), .out(multiplier_6_out));  // open: cin, cout
  Divider #(.width(32)) divider_6 (.a(divider_5_out), .b(32'ha), .out(divider_6_out));  // open: upper, rem
  Subtractor #(.width(32)) subtractor_7 (
    .a(divider_6_out), .b(multiplier_7_out), .out({subtractor_7_out, BCD6}));  // open: bin, bout
  Multiplier #(.width(32)) multiplier_7 (.a(divider_7_out), .b(32'ha), .out(multiplier_7_out));  // open: cin, cout
  Divider #(.width(32)) divider_7 (.a(divider_6_out), .b(32'ha), .out(divider_7_out));  // open: upper, rem
  Subtractor #(.width(32)) subtractor_8 (
    .a(divider_7_out), .b(multiplier_8_out), .out({subtractor_8_out, BCD7}));  // open: bin, bout
  Multiplier #(.width(32)) multiplier_8 (.a(divider_8_out), .b(32'ha), .out(multiplier_8_out));  // open: cin, cout
  Divider #(.width(32)) divider_8 (.a(divider_7_out), .b(32'ha), .out(divider_8_out));  // open: upper, rem
  Subtractor #(.width(32)) subtractor_9 (
    .a(divider_8_out), .b(multiplier_9_out), .out({subtractor_9_out, BCD8}));  // open: bin, bout
  Multiplier #(.width(32)) multiplier_9 (
    .a({divider_9_out, BCD9}), .b(32'ha), .out(multiplier_9_out));  // open: cin, cout
  Divider #(.width(32)) divider_9 (.a(divider_8_out), .b(32'ha), .out({divider_9_out, BCD9}));  // open: upper, rem

  assign Minus = Input[31];
endmodule

module Keypad_Controller (
  input  C,
  input  in_2,
  input  in_3,
  input  in_4,
  input  in_5,
  input  in_6,
  input  _9,
  input  _8,
  input  _7,
  input  _6,
  input  _5,
  input  _4,
  input  _3,
  input  _2,
  input  _1,
  input  _0,
  input  [31:0] From__t9,
  output Write,
  output [31:0] Output
);

  wire iszero_1_out_2, iszero_2_out_2;
  wire [3:0] or_4_out;
  wire [15:0] and_1_out;

  and and_1 (and_1_out[0], C, iszero_1_out_2);
  and and_2 (and_1_out[1], in_2, iszero_1_out_2);
  and and_3 (and_1_out[2], in_3, iszero_1_out_2);
  and and_4 (and_1_out[3], in_4, iszero_1_out_2);
  and and_5 (and_1_out[4], in_5, iszero_1_out_2);
  and and_6 (and_1_out[5], in_6, iszero_1_out_2);
  and and_7 (and_1_out[6], _9, iszero_1_out_2);
  and and_8 (and_1_out[7], _8, iszero_1_out_2);
  and and_9 (and_1_out[8], _7, iszero_1_out_2);
  and and_10 (and_1_out[9], _6, iszero_1_out_2);
  and and_11 (and_1_out[10], _5, iszero_1_out_2);
  and and_12 (and_1_out[11], _4, iszero_1_out_2);
  and and_13 (and_1_out[12], _3, iszero_1_out_2);
  and and_14 (and_1_out[13], _2, iszero_1_out_2);
  and and_15 (and_1_out[14], _1, iszero_1_out_2);
  and and_16 (and_1_out[15], _0, iszero_1_out_2);
  isZero iszero_1 (.Input(From__t9), .out_2(iszero_1_out_2));
  or or_1 (or_4_out[3], and_1_out[0], and_1_out[1], and_1_out[2], and_1_out[3], and_1_out[4], and_1_out[5], and_1_out[6], and_1_out[7]);
  or or_2 (or_4_out[2], and_1_out[8], and_1_out[9], and_1_out[10], and_1_out[11], and_1_out[0], and_1_out[1], and_1_out[2], and_1_out[3]);
  or or_3 (or_4_out[1], and_1_out[12], and_1_out[13], and_1_out[9], and_1_out[8], and_1_out[5], and_1_out[4], and_1_out[1], and_1_out[0]);
  or or_4 (or_4_out[0], and_1_out[12], and_1_out[14], and_1_out[10], and_1_out[8], and_1_out[6], and_1_out[4], and_1_out[2], and_1_out[0]);
  isZero iszero_2 (.Input({{16{1'b0}}, and_1_out}), .out_2(iszero_2_out_2));
  not not_1 (Write, iszero_2_out_2);
  assign Output = Write ? {28'h8000000, or_4_out} : 32'bz;  // Controlled_Buffer controlled_buffer_1
endmodule

module isZero (
  input  [31:0] Input,
  output out_2
);

  wire or_1_out;

  or or_1 (or_1_out, Input[0], Input[1], Input[2], Input[3], Input[4], Input[5], Input[6], Input[7], Input[8], Input[9], Input[10], Input[11], Input[12], Input[13], Input[14], Input[15], Input[16], Input[17], Input[18], Input[19], Input[20], Input[21], Input[22], Input[23], Input[24], Input[25], Input[26], Input[27], Input[28], Input[29], Input[30], Input[31]);
  not not_1 (out_2, or_1_out);
endmodule

module Instruction_Memory__TO_DO (
  input  [31:0] Input,
  output [31:0] Output
);

  ROM #(.addrWidth(16), .dataWidth(32)) rom_1 (.addr(Input[17:2]), .data(Output));  // open: sel

  // Notes on the sheet:
  //   contents of rom_1 (hex, n*v repeats v):
  //   1320ffff 17200000 194820 3129000f 15200000 2928000a 20010001 1028000c 2001000a 10290022 2001000b
  //   10290031 2001000c 10290042 2001000d 10290057 2001000e 10290070 2001000f 1029007b 22100001 4020
  //   2a080002 20010001 10280010 115020 20010000 10280008 11c020 810001e 4020 4820 5020 5820 c820 8100000
  //   200d0001 11400003 216b000a 14d5022 1540fffb 1695820 b8820 810001c 4020 2ae80001 20010000 10280005
  //   114820 8020 119020 20170002 8100029 13c020 139020 8820 20170002 810001e 2329820 b820 8100082 4020
  //   2ae80001 20010000 10280005 114820 8020 119020 20170003 8100029 13c020 139020 8820 20170003 810001e
  //   2329822 4020 1139822 b820 8100082 4020 2ae80001 20010000 10280006 114820 8020 119020 12b020 20170004
  //   8100029 13c020 139020 9820 12b020 8820 20170004 810001e 200d0001 b820 12c0001e 2719820 2cdb022
  //   8100061 4020 2ae80001 20010000 10280006 114820 8020 119020 12a820 20170005 8100029 13c020 139020
  //   9820 12a820 8820 20170005 810001e b820 12320005 232402a 11000006 2519022 22730001 8100078 2519022
  //   22730001 8100078 20010002 1037ffb6 20010003 1037ffc5 20010004 1037ffd9 20010005 1037ffee 13c020
  //   139020 8820 22f70001 810001e c820 c020 8020 8820 9020 9820 b820 810001e
endmodule

module Shift_Left__TO_DO (
  input  [31:0] Input,
  input  [4:0] Shift_Amount,
  output [31:0] Result
);

  Shifter #(.width(32)) shifter_1 (.in(Input), .\dist (Shift_Amount), .out(Result));
endmodule

module Shift_Right__TO_DO (
  input  [31:0] Input,
  input  [4:0] Shift_Amount,
  output [31:0] Result
);

  Shifter #(.width(32), .shift("lr")) shifter_1 (.in(Input), .\dist (Shift_Amount), .out(Result));
endmodule

module Sign_Extend__TO_DO (
  input  [15:0] _16_Bit_Input,
  output [31:0] _32_Bit_Result
);


  assign _32_Bit_Result = {{17{_16_Bit_Input[15]}}, _16_Bit_Input[14:0]};
endmodule

module _32_bit_ALU__TO_DO (
  input  [3:0] ALU_Operation,
  input  [31:0] Input_1,
  input  [31:0] Input_2,
  input  [4:0] Shift_Amount,
  input  [1:0] Shift_Operation,
  output Zero,
  output [31:0] Result
);

  wire [0:0] subtractor_1_out_2;
  wire [30:0] subtractor_1_out;
  wire [31:0] adder_1_out, And_out, multiplexer_2_out, Nor_out, Or_out, Shift_Left_result, Shift_Right_result;

  Adder #(.width(32)) adder_1 (.a(Input_1), .b(Input_2), .out(adder_1_out));  // open: cin, cout
  Subtractor #(.width(32)) subtractor_1 (
    .a(Input_1), .b(Input_2), .out({subtractor_1_out_2[0], subtractor_1_out}));  // open: bin, bout
  Shift_Left__TO_DO Shift_Left (.Input(Input_2), .Shift_Amount(Shift_Amount), .Result(Shift_Left_result));
  Shift_Right__TO_DO Shift_Right (.Input(Input_2), .Shift_Amount(Shift_Amount), .Result(Shift_Right_result));
  assign And_out = Input_1 & Input_2;  // AND_Gate And, 32 bits wide
  assign Or_out = Input_1 | Input_2;  // OR_Gate Or, 32 bits wide
  assign Nor_out = ~(Input_1 | Input_2);  // NOR_Gate Nor, 32 bits wide
  Multiplexer #(.select(2), .width(32), .enable("false")) multiplexer_1 (
    .in0(multiplexer_2_out), .in1(multiplexer_2_out), .in2(Shift_Left_result), .in3(Shift_Right_result),
    .out(Result), .sel(Shift_Operation));
  Multiplexer #(.select(4), .width(32), .enable("false")) multiplexer_2 (
    .in0(And_out), .in1(Or_out), .in2(adder_1_out), .in6({subtractor_1_out_2[0], subtractor_1_out}),
    .in7({{31{1'b0}}, subtractor_1_out_2[0]}), .in12(Nor_out), .out(multiplexer_2_out), .sel(ALU_Operation));  // open: in3, in4, in5, in8, in9, in10, in11, in13, in14, in15
  nor nor_2 (Zero, subtractor_1_out[0], subtractor_1_out[1], subtractor_1_out[2], subtractor_1_out[3], subtractor_1_out[4], subtractor_1_out[5], subtractor_1_out[6], subtractor_1_out[7], subtractor_1_out[8], subtractor_1_out[9], subtractor_1_out[10], subtractor_1_out[11], subtractor_1_out[12], subtractor_1_out[13], subtractor_1_out[14], subtractor_1_out[15], subtractor_1_out[16], subtractor_1_out[17], subtractor_1_out[18], subtractor_1_out[19], subtractor_1_out[20], subtractor_1_out[21], subtractor_1_out[22], subtractor_1_out[23], subtractor_1_out[24], subtractor_1_out[25], subtractor_1_out[26], subtractor_1_out[27], subtractor_1_out[28], subtractor_1_out[29], subtractor_1_out[30], subtractor_1_out_2[0]);
endmodule

module Register_File__TO_DO (
  input  RegWrite,
  input  [4:0] Read_Register_1,
  input  [4:0] Write_Register,
  input  Clock,
  input  [31:0] Write_Data___t9,
  input  [31:0] Write_Data,
  input  Write_Signal,
  input  [4:0] Read_Register_2,
  output [31:0] Read_Data_1,
  output [31:0] t8,
  output [31:0] t9,
  output [31:0] Read_Data_2
);

  wire and_1_out, and_2_out, and_3_out, and_4_out, and_5_out, and_6_out, and_7_out, and_8_out, and_9_out,
       and_10_out, and_11_out, and_12_out, and_13_out, and_14_out, and_15_out, and_16_out, and_17_out,
       and_18_out, and_19_out, and_20_out, and_21_out, and_22_out, and_23_out, and_24_out, and_25_out,
       and_26_out, and_27_out, and_28_out, and_29_out, and_30_out, and_31_out, controlled_buffer_3_out,
       decoder_1_out1, decoder_1_out2, decoder_1_out3, decoder_1_out4, decoder_1_out5, decoder_1_out6,
       decoder_1_out7, decoder_1_out8, decoder_1_out9, decoder_1_out10, decoder_1_out11, decoder_1_out12,
       decoder_1_out13, decoder_1_out14, decoder_1_out15, decoder_1_out16, decoder_1_out17, decoder_1_out18,
       decoder_1_out19, decoder_1_out20, decoder_1_out21, decoder_1_out22, decoder_1_out23, decoder_1_out24,
       decoder_1_out25, decoder_1_out26, decoder_1_out27, decoder_1_out28, decoder_1_out29, decoder_1_out30,
       decoder_1_out31;
  wire [31:0] controlled_buffer_1_out, register_1_q, register_2_q, register_3_q, register_4_q, register_5_q,
       register_6_q, register_7_q, register_8_q, register_9_q, register_10_q, register_11_q, register_12_q,
       register_13_q, register_14_q, register_15_q, register_16_q, register_17_q, register_18_q,
       register_19_q, register_20_q, register_21_q, register_22_q, register_23_q, register_26_q,
       register_27_q, register_28_q, register_29_q, register_30_q, register_31_q;

  Decoder #(.select(5), .enable("false")) decoder_1 (
    .out1(decoder_1_out1), .out2(decoder_1_out2), .out3(decoder_1_out3), .out4(decoder_1_out4),
    .out5(decoder_1_out5), .out6(decoder_1_out6), .out7(decoder_1_out7), .out8(decoder_1_out8),
    .out9(decoder_1_out9), .out10(decoder_1_out10), .out11(decoder_1_out11), .out12(decoder_1_out12),
    .out13(decoder_1_out13), .out14(decoder_1_out14), .out15(decoder_1_out15), .out16(decoder_1_out16),
    .out17(decoder_1_out17), .out18(decoder_1_out18), .out19(decoder_1_out19), .out20(decoder_1_out20),
    .out21(decoder_1_out21), .out22(decoder_1_out22), .out23(decoder_1_out23), .out24(decoder_1_out24),
    .out25(decoder_1_out25), .out26(decoder_1_out26), .out27(decoder_1_out27), .out28(decoder_1_out28),
    .out29(decoder_1_out29), .out30(decoder_1_out30), .out31(decoder_1_out31), .sel(Write_Register));  // open: out0
  assign controlled_buffer_1_out = and_25_out ? Write_Data : 32'bz;  // Controlled_Buffer controlled_buffer_1
  assign controlled_buffer_1_out = Write_Signal ? Write_Data___t9 : 32'bz;  // Controlled_Buffer controlled_buffer_2
  assign controlled_buffer_3_out = and_25_out ? and_25_out : 1'bz;  // Controlled_Buffer controlled_buffer_3
  assign controlled_buffer_3_out = Write_Signal ? Write_Signal : 1'bz;  // Controlled_Buffer controlled_buffer_4
  and and_1 (and_1_out, RegWrite, decoder_1_out1);
  and and_2 (and_2_out, RegWrite, decoder_1_out2);
  and and_3 (and_3_out, RegWrite, decoder_1_out3);
  and and_4 (and_4_out, RegWrite, decoder_1_out4);
  and and_5 (and_5_out, RegWrite, decoder_1_out5);
  and and_6 (and_6_out, RegWrite, decoder_1_out6);
  and and_7 (and_7_out, RegWrite, decoder_1_out7);
  and and_8 (and_8_out, RegWrite, decoder_1_out8);
  and and_9 (and_9_out, RegWrite, decoder_1_out9);
  and and_10 (and_10_out, RegWrite, decoder_1_out10);
  and and_11 (and_11_out, RegWrite, decoder_1_out11);
  and and_12 (and_12_out, RegWrite, decoder_1_out12);
  and and_13 (and_13_out, RegWrite, decoder_1_out13);
  and and_14 (and_14_out, RegWrite, decoder_1_out14);
  and and_15 (and_15_out, RegWrite, decoder_1_out15);
  and and_16 (and_16_out, RegWrite, decoder_1_out16);
  and and_17 (and_17_out, RegWrite, decoder_1_out17);
  and and_18 (and_18_out, RegWrite, decoder_1_out18);
  and and_19 (and_19_out, RegWrite, decoder_1_out19);
  and and_20 (and_20_out, RegWrite, decoder_1_out20);
  and and_21 (and_21_out, RegWrite, decoder_1_out21);
  and and_22 (and_22_out, RegWrite, decoder_1_out22);
  and and_23 (and_23_out, RegWrite, decoder_1_out23);
  and and_24 (and_24_out, RegWrite, decoder_1_out24);
  and and_25 (and_25_out, RegWrite, decoder_1_out25);
  and and_26 (and_26_out, RegWrite, decoder_1_out26);
  and and_27 (and_27_out, RegWrite, decoder_1_out27);
  and and_28 (and_28_out, RegWrite, decoder_1_out28);
  and and_29 (and_29_out, RegWrite, decoder_1_out29);
  and and_30 (and_30_out, RegWrite, decoder_1_out30);
  and and_31 (and_31_out, RegWrite, decoder_1_out31);
  Register #(.width(32)) register_1 (.D(Write_Data), .en(and_1_out), .Q(register_1_q), .clk(Clock));  // open: clr
  Register #(.width(32)) register_2 (.D(Write_Data), .en(and_2_out), .Q(register_2_q), .clk(Clock));  // open: clr
  Register #(.width(32)) register_3 (.D(Write_Data), .en(and_3_out), .Q(register_3_q), .clk(Clock));  // open: clr
  Register #(.width(32)) register_4 (.D(Write_Data), .en(and_4_out), .Q(register_4_q), .clk(Clock));  // open: clr
  Register #(.width(32)) register_5 (.D(Write_Data), .en(and_5_out), .Q(register_5_q), .clk(Clock));  // open: clr
  Register #(.width(32)) register_6 (.D(Write_Data), .en(and_6_out), .Q(register_6_q), .clk(Clock));  // open: clr
  Register #(.width(32)) register_7 (.D(Write_Data), .en(and_7_out), .Q(register_7_q), .clk(Clock));  // open: clr
  Register #(.width(32)) register_8 (.D(Write_Data), .en(and_8_out), .Q(register_8_q), .clk(Clock));  // open: clr
  Register #(.width(32)) register_9 (.D(Write_Data), .en(and_9_out), .Q(register_9_q), .clk(Clock));  // open: clr
  Register #(.width(32)) register_10 (.D(Write_Data), .en(and_10_out), .Q(register_10_q), .clk(Clock));  // open: clr
  Register #(.width(32)) register_11 (.D(Write_Data), .en(and_11_out), .Q(register_11_q), .clk(Clock));  // open: clr
  Register #(.width(32)) register_12 (.D(Write_Data), .en(and_12_out), .Q(register_12_q), .clk(Clock));  // open: clr
  Register #(.width(32)) register_13 (.D(Write_Data), .en(and_13_out), .Q(register_13_q), .clk(Clock));  // open: clr
  Register #(.width(32)) register_14 (.D(Write_Data), .en(and_14_out), .Q(register_14_q), .clk(Clock));  // open: clr
  Register #(.width(32)) register_15 (.D(Write_Data), .en(and_15_out), .Q(register_15_q), .clk(Clock));  // open: clr
  Register #(.width(32)) register_16 (.D(Write_Data), .en(and_16_out), .Q(register_16_q), .clk(Clock));  // open: clr
  Register #(.width(32)) register_17 (.D(Write_Data), .en(and_17_out), .Q(register_17_q), .clk(Clock));  // open: clr
  Register #(.width(32)) register_18 (.D(Write_Data), .en(and_18_out), .Q(register_18_q), .clk(Clock));  // open: clr
  Register #(.width(32)) register_19 (.D(Write_Data), .en(and_19_out), .Q(register_19_q), .clk(Clock));  // open: clr
  Register #(.width(32)) register_20 (.D(Write_Data), .en(and_20_out), .Q(register_20_q), .clk(Clock));  // open: clr
  Register #(.width(32)) register_21 (.D(Write_Data), .en(and_21_out), .Q(register_21_q), .clk(Clock));  // open: clr
  Register #(.width(32)) register_22 (.D(Write_Data), .en(and_22_out), .Q(register_22_q), .clk(Clock));  // open: clr
  Register #(.width(32)) register_23 (.D(Write_Data), .en(and_23_out), .Q(register_23_q), .clk(Clock));  // open: clr
  Register #(.width(32)) register_24 (.D(Write_Data), .en(and_24_out), .Q(t8), .clk(Clock));  // open: clr
  Register #(.width(32)) register_25 (
    .D(controlled_buffer_1_out), .en(controlled_buffer_3_out), .Q(t9), .clk(Clock));  // open: clr
  Register #(.width(32)) register_26 (.D(Write_Data), .en(and_26_out), .Q(register_26_q), .clk(Clock));  // open: clr
  Register #(.width(32)) register_27 (.D(Write_Data), .en(and_27_out), .Q(register_27_q), .clk(Clock));  // open: clr
  Register #(.width(32)) register_28 (.D(Write_Data), .en(and_28_out), .Q(register_28_q), .clk(Clock));  // open: clr
  Register #(.width(32)) register_29 (.D(Write_Data), .en(and_29_out), .Q(register_29_q), .clk(Clock));  // open: clr
  Register #(.width(32)) register_30 (.D(Write_Data), .en(and_30_out), .Q(register_30_q), .clk(Clock));  // open: clr
  Register #(.width(32)) register_31 (.D(Write_Data), .en(and_31_out), .Q(register_31_q), .clk(Clock));  // open: clr
  Multiplexer #(.select(5), .width(32), .enable("false")) multiplexer_1 (
    .in0({32{1'b0}}), .in1(register_1_q), .in2(register_2_q), .in3(register_3_q), .in4(register_4_q),
    .in5(register_5_q), .in6(register_6_q), .in7(register_7_q), .in8(register_8_q), .in9(register_9_q),
    .in10(register_10_q), .in11(register_11_q), .in12(register_12_q), .in13(register_13_q),
    .in14(register_14_q), .in15(register_15_q), .in16(register_16_q), .in17(register_17_q),
    .in18(register_18_q), .in19(register_19_q), .in20(register_20_q), .in21(register_21_q),
    .in22(register_22_q), .in23(register_23_q), .in24(t8), .in25(t9), .in26(register_26_q),
    .in27(register_27_q), .in28(register_28_q), .in29(register_29_q), .in30(register_30_q),
    .in31(register_31_q), .out(Read_Data_1), .sel(Read_Register_1));
  Multiplexer #(.select(5), .width(32), .enable("false")) multiplexer_2 (
    .in0({32{1'b0}}), .in1(register_1_q), .in2(register_2_q), .in3(register_3_q), .in4(register_4_q),
    .in5(register_5_q), .in6(register_6_q), .in7(register_7_q), .in8(register_8_q), .in9(register_9_q),
    .in10(register_10_q), .in11(register_11_q), .in12(register_12_q), .in13(register_13_q),
    .in14(register_14_q), .in15(register_15_q), .in16(register_16_q), .in17(register_17_q),
    .in18(register_18_q), .in19(register_19_q), .in20(register_20_q), .in21(register_21_q),
    .in22(register_22_q), .in23(register_23_q), .in24(t8), .in25(t9), .in26(register_26_q),
    .in27(register_27_q), .in28(register_28_q), .in29(register_29_q), .in30(register_30_q),
    .in31(register_31_q), .out(Read_Data_2), .sel(Read_Register_2));
endmodule

module Control_Unit__TO_DO (
  input  [5:0] Opcode,
  output [5:0] Immediate_Functions,
  output Register_Destination,
  output Jump,
  output Register_Write,
  output Branch_Equal,
  output Branch_Not_Equal,
  output ALU_Source,
  output [1:0] ALU_Operation
);

  wire not_1_out, not_2_out, not_3_out, not_4_out, not_5_out, not_6_out, not_7_out, not_8_out, not_9_out,
       not_10_out, not_11_out, not_12_out, not_13_out, not_14_out, not_15_out, not_16_out, not_17_out,
       not_18_out, not_19_out, not_20_out, not_21_out, not_22_out, not_23_out, not_24_out, not_25_out,
       not_26_out, not_27_out, not_28_out, not_29_out, not_30_out, not_31_out, not_32_out, not_33_out,
       not_34_out, not_35_out, not_36_out, not_53_out, not_54_out, not_55_out;
  wire [5:0] multiplexer_1_out, multiplexer_2_out, multiplexer_3_out, multiplexer_4_out, not_41_out,
       not_45_out, not_51_out;
  wire [5:1] not_48_out;

  not not_1 (not_1_out, Opcode[5]);
  not not_2 (not_2_out, Opcode[4]);
  not not_3 (not_3_out, Opcode[2]);
  not not_4 (not_4_out, Opcode[1]);
  not not_5 (not_5_out, Opcode[0]);
  not not_6 (not_6_out, Opcode[5]);
  not not_7 (not_7_out, Opcode[4]);
  not not_8 (not_8_out, Opcode[1]);
  not not_9 (not_9_out, Opcode[0]);
  not not_10 (not_10_out, Opcode[5]);
  not not_11 (not_11_out, Opcode[4]);
  not not_12 (not_12_out, Opcode[1]);
  not not_13 (not_13_out, Opcode[5]);
  not not_14 (not_14_out, Opcode[4]);
  not not_15 (not_15_out, Opcode[2]);
  not not_16 (not_16_out, Opcode[0]);
  not not_17 (not_17_out, Opcode[5]);
  not not_18 (not_18_out, Opcode[4]);
  not not_19 (not_19_out, Opcode[3]);
  not not_20 (not_20_out, Opcode[2]);
  not not_21 (not_21_out, Opcode[1]);
  not not_22 (not_22_out, Opcode[0]);
  not not_23 (not_23_out, Opcode[5]);
  not not_24 (not_24_out, Opcode[4]);
  not not_25 (not_25_out, Opcode[3]);
  not not_26 (not_26_out, Opcode[2]);
  not not_27 (not_27_out, Opcode[0]);
  not not_28 (not_28_out, Opcode[5]);
  not not_29 (not_29_out, Opcode[4]);
  not not_30 (not_30_out, Opcode[3]);
  not not_31 (not_31_out, Opcode[1]);
  not not_32 (not_32_out, Opcode[0]);
  not not_33 (not_33_out, Opcode[5]);
  not not_34 (not_34_out, Opcode[4]);
  not not_35 (not_35_out, Opcode[3]);
  not not_36 (not_36_out, Opcode[1]);
  and Addi (not_41_out[5], not_1_out, not_2_out, Opcode[3], not_3_out, not_4_out, not_5_out);
  and Andi (not_45_out[5], not_6_out, not_7_out, Opcode[3], Opcode[2], not_8_out, not_9_out);
  and Ori (not_48_out[5], not_10_out, not_11_out, Opcode[3], Opcode[2], not_12_out, Opcode[0]);
  and Slti (not_51_out[5], not_13_out, not_14_out, Opcode[3], not_15_out, Opcode[1], not_16_out);
  and And (Register_Destination, not_17_out, not_18_out, not_19_out, not_20_out, not_21_out, not_22_out);
  and u_JUMP (Jump, not_23_out, not_24_out, not_25_out, not_26_out, Opcode[1], not_27_out);
  and BEQ (Branch_Equal, not_28_out, not_29_out, not_30_out, Opcode[2], not_31_out, not_32_out);
  and BNE (Branch_Not_Equal, not_33_out, not_34_out, not_35_out, Opcode[2], not_36_out, Opcode[0]);
  not not_37 (not_41_out[4], not_41_out[5]);
  not not_38 (not_41_out[3], not_41_out[5]);
  not not_39 (not_41_out[2], not_41_out[5]);
  not not_40 (not_41_out[1], not_41_out[5]);
  not not_41 (not_41_out[0], not_41_out[5]);
  not not_42 (not_45_out[4], not_45_out[5]);
  not not_43 (not_45_out[3], not_45_out[5]);
  not not_44 (not_45_out[1], not_45_out[5]);
  not not_45 (not_45_out[0], not_45_out[5]);
  not not_46 (not_48_out[4], not_48_out[5]);
  not not_47 (not_48_out[3], not_48_out[5]);
  not not_48 (not_48_out[1], not_48_out[5]);
  not not_49 (not_51_out[4], not_51_out[5]);
  not not_50 (not_51_out[2], not_51_out[5]);
  not not_51 (not_51_out[0], not_51_out[5]);
  not not_52 (ALU_Operation[1], ALU_Operation[0]);
  or or_1 (ALU_Operation[0], Branch_Equal, Branch_Not_Equal);
  Multiplexer #(.width(6), .enable("false")) multiplexer_1 (
    .in0({6{1'b0}}), .in1({not_51_out[5:4], not_51_out[5], not_51_out[2], not_51_out[5], not_51_out[0]}),
    .out(multiplexer_1_out), .sel(not_51_out[5]));
  not not_53 (not_53_out, Jump);
  not not_54 (not_54_out, Branch_Equal);
  not not_55 (not_55_out, Branch_Not_Equal);
  Multiplexer #(.width(6), .enable("false")) multiplexer_2 (
    .in0(multiplexer_1_out), .in1({not_48_out[5:3], not_48_out[5], not_48_out[1], not_48_out[5]}),
    .out(multiplexer_2_out), .sel(not_48_out[5]));
  Multiplexer #(.width(6), .enable("false")) multiplexer_3 (
    .in0(multiplexer_2_out), .in1({not_45_out[5:3], not_45_out[5], not_45_out[1:0]}),
    .out(multiplexer_3_out), .sel(not_45_out[5]));
  Multiplexer #(.width(6), .enable("false")) multiplexer_4 (
    .in0(multiplexer_3_out), .in1(not_41_out), .out(multiplexer_4_out), .sel(not_41_out[5]));
  and And_2 (Register_Write, not_53_out, not_54_out, not_55_out);
  Multiplexer #(.width(6), .enable("false")) multiplexer_5 (
    .in0({6{1'b0}}), .in1(multiplexer_4_out), .out(Immediate_Functions), .sel(Opcode[3]));

  assign ALU_Source = Opcode[3];
endmodule

module Shift_Left_Two (
  input  [31:0] Input,
  output [31:0] Result
);

  Shifter #(.width(32)) shifter_1 (.in(Input), .\dist (5'b00010), .out(Result));
endmodule

module Overflow_Detection (
  input  [31:0] A,
  input  [31:0] B,
  input  [31:0] Result,
  output Overflow
);

  wire and_1_out, and_2_out, and_3_out, and_4_out, not_1_out, not_2_out, not_3_out, not_4_out, not_5_out,
       not_6_out, or_1_out, or_2_out;

  not not_1 (not_1_out, A[31]);
  not not_2 (not_2_out, B[31]);
  not not_3 (not_3_out, Result[31]);
  not not_4 (not_4_out, B[31]);
  not not_5 (not_5_out, A[31]);
  not not_6 (not_6_out, Result[31]);
  and and_1 (and_1_out, not_1_out, not_2_out, Result[31]);
  and and_2 (and_2_out, A[31], B[31], not_3_out);
  and and_3 (and_3_out, A[31], not_4_out, Result[31]);
  and and_4 (and_4_out, not_5_out, B[31], not_6_out);
  or or_1 (or_1_out, and_1_out, and_2_out);
  or or_2 (or_2_out, and_3_out, and_4_out);
  or or_3 (Overflow, or_1_out, or_2_out);
endmodule

module ALU_Control (
  input  [1:0] ALU_Operation_Input,
  input  [5:0] Function,
  output [3:0] ALU_Operation,
  output [1:0] Shift_Operation
);

  wire and_2_out, and_out, not_1_out, not_2_out, not_3_out, not_4_out, not_5_out, not_6_out, not_7_out,
       not_8_out, not_9_out, not_10_out, not_11_out, not_12_out, not_13_out, not_14_out, not_15_out,
       not_16_out, not_17_out, not_18_out, not_19_out, not_20_out, not_21_out, not_22_out, not_23_out,
       not_24_out, not_25_out, not_26_out, not_27_out, not_28_out, not_29_out, not_30_out, not_31_out,
       not_32_out, not_33_out, not_34_out, not_35_out, not_36_out, not_57_out;
  wire [1:0] multiplexer_1_out, not_37_out, not_54_out;
  wire [1:1] and_4_out;
  wire [3:0] multiplexer_2_out, multiplexer_4_out, multiplexer_5_out, multiplexer_6_out, multiplexer_7_out,
       multiplexer_8_out, multiplexer_10_out, not_40_out, not_44_out, not_46_out, not_51_out, not_56_out,
       or_out;
  wire [3:2] slt_out;

  not not_1 (not_1_out, Function[4]);
  not not_2 (not_2_out, Function[3]);
  not not_3 (not_3_out, Function[2]);
  not not_4 (not_4_out, Function[1]);
  not not_5 (not_5_out, Function[0]);
  not not_6 (not_6_out, Function[4]);
  not not_7 (not_7_out, Function[3]);
  not not_8 (not_8_out, Function[1]);
  not not_9 (not_9_out, Function[0]);
  not not_10 (not_10_out, Function[4]);
  not not_11 (not_11_out, Function[3]);
  not not_12 (not_12_out, Function[2]);
  not not_13 (not_13_out, Function[0]);
  not not_14 (not_14_out, ALU_Operation_Input[1]);
  not not_15 (not_15_out, Function[4]);
  not not_16 (not_16_out, Function[3]);
  not not_17 (not_17_out, Function[1]);
  not not_18 (not_18_out, Function[4]);
  not not_19 (not_19_out, Function[3]);
  not not_20 (not_20_out, Function[4]);
  not not_21 (not_21_out, Function[2]);
  not not_22 (not_22_out, Function[0]);
  not not_23 (not_23_out, ALU_Operation_Input[1]);
  not not_24 (not_24_out, ALU_Operation_Input[0]);
  not not_25 (not_25_out, Function[5]);
  not not_26 (not_26_out, Function[5]);
  not not_27 (not_27_out, Function[4]);
  not not_28 (not_28_out, Function[3]);
  not not_29 (not_29_out, Function[2]);
  not not_30 (not_30_out, Function[1]);
  not not_31 (not_31_out, Function[0]);
  not not_32 (not_32_out, Function[5]);
  not not_33 (not_33_out, Function[4]);
  not not_34 (not_34_out, Function[3]);
  not not_35 (not_35_out, Function[2]);
  not not_36 (not_36_out, Function[0]);
  and add (not_40_out[1], Function[5], not_1_out, not_2_out, not_3_out, not_4_out, not_5_out);
  and \and  (and_out, Function[5], not_6_out, not_7_out, Function[2], not_8_out, not_9_out);
  and sub (not_56_out[2], Function[5], not_10_out, not_11_out, not_12_out, Function[1], not_13_out);
  and Branch (not_46_out[2], not_14_out, ALU_Operation_Input[0]);
  and \or  (or_out[0], Function[5], not_15_out, not_16_out, Function[2], not_17_out, Function[0]);
  and \nor  (not_51_out[3], Function[5], not_18_out, not_19_out, Function[2], Function[1], Function[0]);
  and slt (slt_out[2], Function[5], not_20_out, Function[3], not_21_out, Function[1], not_22_out);
  and and_2 (and_2_out, not_23_out, not_24_out, not_25_out);
  not not_37 (not_37_out[0], not_37_out[1]);
  and and_3 (not_37_out[1], not_26_out, not_27_out, not_28_out, not_29_out, not_30_out, not_31_out);
  and and_4 (and_4_out[1], not_32_out, not_33_out, not_34_out, not_35_out, Function[1], not_36_out);
  not not_38 (not_40_out[3], not_40_out[1]);
  not not_39 (not_40_out[2], not_40_out[1]);
  not not_40 (not_40_out[0], not_40_out[1]);
  not not_41 (not_44_out[3], and_out);
  not not_42 (not_44_out[2], and_out);
  not not_43 (not_44_out[1], and_out);
  not not_44 (not_44_out[0], and_out);
  not not_45 (not_46_out[3], not_46_out[2]);
  not not_46 (not_46_out[0], not_46_out[2]);
  not not_47 (or_out[3], or_out[0]);
  not not_48 (or_out[2], or_out[0]);
  not not_49 (or_out[1], or_out[0]);
  not not_50 (not_51_out[1], not_51_out[3]);
  not not_51 (not_51_out[0], not_51_out[3]);
  not not_52 (slt_out[3], slt_out[2]);
  not not_53 (not_54_out[1], and_2_out);
  not not_54 (not_54_out[0], and_2_out);
  not not_55 (not_56_out[3], not_56_out[2]);
  not not_56 (not_56_out[0], not_56_out[2]);
  not not_57 (not_57_out, and_2_out);
  Multiplexer #(.width(2), .enable("false")) multiplexer_1 (
    .in0(not_37_out), .in1({2{and_4_out[1]}}), .out(multiplexer_1_out), .sel(Function[1]));
  Multiplexer #(.width(4), .enable("false")) multiplexer_2 (
    .in0(4'b0000), .in1({slt_out, {2{slt_out[2]}}}), .out(multiplexer_2_out), .sel(slt_out[2]));
  Multiplexer #(.width(2), .enable("false")) multiplexer_3 (
    .in0(not_54_out), .in1(multiplexer_1_out), .out(Shift_Operation), .sel(not_57_out));
  Multiplexer #(.width(4), .enable("false")) multiplexer_4 (
    .in0(multiplexer_2_out), .in1({{2{not_51_out[3]}}, not_51_out[1:0]}), .out(multiplexer_4_out),
    .sel(not_51_out[3]));
  Multiplexer #(.width(4), .enable("false")) multiplexer_5 (
    .in0(multiplexer_4_out), .in1(or_out), .out(multiplexer_5_out), .sel(or_out[0]));
  Multiplexer #(.width(4), .enable("false")) multiplexer_6 (
    .in0(multiplexer_5_out), .in1({not_56_out[3:2], not_56_out[2], not_56_out[0]}), .out(multiplexer_6_out),
    .sel(not_56_out[2]));
  Multiplexer #(.width(4), .enable("false")) multiplexer_7 (
    .in0(multiplexer_6_out), .in1(not_44_out), .out(multiplexer_7_out), .sel(and_out));
  Multiplexer #(.width(4), .enable("false")) multiplexer_8 (
    .in0(multiplexer_7_out), .in1(not_40_out), .out(multiplexer_8_out), .sel(not_40_out[1]));
  Multiplexer #(.width(4), .enable("false")) multiplexer_9 (
    .in0(multiplexer_10_out), .in1(multiplexer_8_out), .out(ALU_Operation), .sel(ALU_Operation_Input[1]));
  Multiplexer #(.width(4), .enable("false")) multiplexer_10 (
    .in0(4'b0000), .in1({not_46_out[3:2], not_46_out[2], not_46_out[0]}), .out(multiplexer_10_out),
    .sel(not_46_out[2]));
endmodule
